// Logisim project circuito_final.circ as structural Verilog: 3 circuits, main circuit main
module main (
  input  CLR,
  input  Q3,
  input  Q2,
  input  Q1,
  input  Q0
);

  wire cont_1_out_2, cont_1_out_3, cont_1_out_4, cont_1_out_5, n011_1_s0, n011_1_s1, n011_1_s2, n011_1_s3,
       n011_1_s4, n011_1_s5, n011_1_s6, n011_1_s7, n011_1_s8, n011_1_s9, n011_1_s10, n011_1_s11, n011_1_s12,
       n011_1_s13, n011_1_s14, n011_1_s15, n011_1_s16, n011_1_s17, n011_1_s18, n011_1_s19, or_1_out,
       or_2_out, or_3_out, or_4_out;

  cont cont_1 (.in_1(CLR), .out_2(cont_1_out_2), .out_3(cont_1_out_3), .out_4(cont_1_out_4), .out_5(cont_1_out_5));
  or or_1 (or_1_out, Q3, cont_1_out_5);
  or or_2 (or_2_out, Q2, cont_1_out_4);
  or or_3 (or_3_out, Q1, cont_1_out_3);
  or or_4 (or_4_out, Q0, cont_1_out_2);
  _011 u_011_1 (
    .Q3(or_1_out), .Q2(or_2_out), .Q1(or_3_out), .Q0(or_4_out), .S0(n011_1_s0), .S1(n011_1_s1),
    .S2(n011_1_s2), .S3(n011_1_s3), .S4(n011_1_s4), .S5(n011_1_s5), .S6(n011_1_s6), .S7(n011_1_s7),
    .S8(n011_1_s8), .S9(n011_1_s9), .S10(n011_1_s10), .S11(n011_1_s11), .S12(n011_1_s12), .S13(n011_1_s13),
    .S14(n011_1_s14), .S15(n011_1_s15), .S16(n011_1_s16), .S17(n011_1_s17), .S18(n011_1_s18), .S19(n011_1_s19));
  LED led_1 (.in(n011_1_s0));
  LED led_2 (.in(n011_1_s4));
  LED led_3 (.in(n011_1_s8));
  LED led_4 (.in(n011_1_s12));
  LED led_5 (.in(n011_1_s16));
  LED led_6 (.in(n011_1_s1));
  LED led_7 (.in(n011_1_s2));
  LED led_8 (.in(n011_1_s3));
  LED led_9 (.in(n011_1_s5));
  LED led_10 (.in(n011_1_s6));
  LED led_11 (.in(n011_1_s7));
  LED led_12 (.in(n011_1_s9));
  LED led_13 (.in(n011_1_s10));
  LED led_14 (.in(n011_1_s11));
  LED led_15 (.in(n011_1_s15));
  LED led_16 (.in(n011_1_s13));
  LED led_17 (.in(n011_1_s14));
  LED led_18 (.in(n011_1_s19));
  LED led_19 (.in(n011_1_s18));
  LED led_20 (.in(n011_1_s17));

  // Notes on the sheet:
  //   5
  //   0
  //   4
  //   8
  //   9
  //   12
  //   16
  //   13
  //   6
  //   1
  //   2
  //   3
  //   17
  //   18
  //   14
  //   7
  //   11
  //   15
  //   10
  //   19
endmodule

module _011 (
  input  Q3,
  input  Q2,
  input  Q1,
  input  Q0,
  output S0,
  output S1,
  output S2,
  output S3,
  output S4,
  output S5,
  output S6,
  output S7,
  output S8,
  output S9,
  output S10,
  output S11,
  output S12,
  output S13,
  output S14,
  output S15,
  output S16,
  output S17,
  output S18,
  output S19
);

  wire and_1_out, and_2_out, and_3_out, and_4_out, and_5_out, and_6_out, and_7_out, and_8_out, and_9_out,
       and_10_out, and_11_out, and_12_out, and_13_out, and_14_out, and_15_out, and_16_out, and_17_out,
       and_18_out, and_19_out, and_20_out, and_21_out, and_22_out, and_23_out, and_24_out, and_25_out,
       and_26_out, and_27_out, and_28_out, and_29_out, and_30_out, and_31_out, and_32_out, and_33_out,
       and_34_out, and_35_out, and_36_out, and_37_out, and_38_out, and_39_out, and_40_out, and_41_out,
       and_42_out, and_43_out, and_44_out, and_45_out, and_46_out, and_47_out, and_48_out, and_49_out,
       and_50_out, and_51_out, and_52_out, and_53_out, and_54_out, and_56_out, and_57_out, and_58_out,
       and_59_out, and_60_out, and_61_out, and_62_out, and_63_out, and_64_out, and_65_out, and_66_out,
       and_67_out, and_68_out, and_69_out, not_1_out, not_2_out, not_3_out, not_4_out, not_5_out, not_6_out,
       not_7_out, not_8_out, not_9_out, not_10_out, not_11_out, not_12_out, not_13_out, not_14_out,
       not_15_out, not_16_out, not_17_out, not_18_out, not_19_out, not_20_out, not_21_out, not_22_out,
       not_23_out, not_24_out, not_25_out, not_26_out, not_27_out, not_28_out, not_29_out, not_30_out,
       not_31_out, not_32_out, not_33_out, not_34_out, not_35_out, not_36_out, not_37_out, not_38_out,
       not_39_out, not_40_out, not_41_out, not_42_out, not_43_out, not_44_out, not_45_out, not_46_out,
       not_47_out, not_48_out, not_49_out, not_50_out, not_51_out, not_52_out, not_53_out, not_54_out,
       not_55_out, not_56_out, not_57_out, not_58_out, not_59_out, not_60_out, not_61_out, not_62_out,
       not_63_out, not_64_out, not_65_out, not_66_out, not_67_out, not_68_out, not_69_out, not_70_out,
       not_71_out, not_72_out, not_73_out, not_74_out, not_75_out, not_76_out, not_77_out, not_78_out,
       not_79_out, not_80_out, not_81_out, not_82_out, not_83_out, not_84_out, not_85_out, not_86_out,
       not_87_out, not_88_out, not_89_out, not_90_out, not_91_out;

  and and_1 (and_1_out, Q1, Q0);
  and and_2 (and_2_out, Q2, Q0);
  and and_3 (and_3_out, Q3, Q2, Q1);
  not not_1 (not_1_out, Q2);
  and and_4 (and_4_out, not_1_out, not_2_out);
  not not_2 (not_2_out, Q0);
  and and_5 (and_5_out, Q2, Q0);
  not not_3 (not_3_out, Q3);
  and and_6 (and_6_out, not_3_out, Q2, not_4_out);
  not not_4 (not_4_out, Q1);
  not not_5 (not_5_out, Q3);
  and and_7 (and_7_out, not_5_out, Q2, Q0);
  and and_8 (and_8_out, Q3, Q2, Q1);
  not not_6 (not_6_out, Q2);
  and and_9 (and_9_out, not_6_out, not_7_out);
  not not_7 (not_7_out, Q0);
  and and_10 (and_10_out, Q1, not_8_out);
  not not_8 (not_8_out, Q0);
  and and_11 (and_11_out, Q2, Q0);
  not not_9 (not_9_out, Q3);
  not not_10 (not_10_out, Q2);
  not not_11 (not_11_out, Q1);
  not not_12 (not_12_out, Q3);
  not not_13 (not_13_out, Q1);
  not not_14 (not_14_out, Q0);
  not not_15 (not_15_out, Q3);
  not not_16 (not_16_out, Q2);
  not not_17 (not_17_out, Q1);
  not not_18 (not_18_out, Q1);
  and and_12 (and_12_out, not_18_out, not_19_out);
  not not_19 (not_19_out, Q0);
  not not_20 (not_20_out, Q2);
  and and_13 (and_13_out, not_20_out, Q1);
  not not_21 (not_21_out, Q3);
  and and_14 (and_14_out, not_21_out, Q1, Q0);
  and and_15 (and_15_out, Q3, not_22_out);
  not not_22 (not_22_out, Q1);
  not not_23 (not_23_out, Q3);
  and and_16 (and_16_out, not_23_out, not_24_out, not_25_out);
  not not_24 (not_24_out, Q1);
  not not_25 (not_25_out, Q0);
  not not_26 (not_26_out, Q2);
  and and_17 (and_17_out, not_26_out, Q1, Q0);
  and and_18 (and_18_out, Q2, not_27_out);
  not not_27 (not_27_out, Q1);
  and and_19 (and_19_out, Q2, not_28_out);
  not not_28 (not_28_out, Q0);
  and and_20 (and_20_out, Q3, Q0);
  and and_21 (and_21_out, Q3, Q1);
  not not_29 (not_29_out, Q2);
  not not_30 (not_30_out, Q3);
  not not_31 (not_31_out, Q1);
  not not_32 (not_32_out, Q0);
  not not_33 (not_33_out, Q2);
  not not_34 (not_34_out, Q3);
  and and_22 (and_22_out, not_34_out, Q0);
  and and_23 (and_23_out, Q3, not_35_out);
  not not_35 (not_35_out, Q2);
  not not_36 (not_36_out, Q3);
  and and_24 (and_24_out, not_36_out, not_37_out, not_38_out);
  not not_37 (not_37_out, Q1);
  not not_38 (not_38_out, Q0);
  not not_39 (not_39_out, Q3);
  and and_25 (and_25_out, not_39_out, Q2, not_40_out);
  not not_40 (not_40_out, Q0);
  and and_26 (and_26_out, Q3, not_41_out, Q0);
  not not_41 (not_41_out, Q1);
  and and_27 (and_27_out, Q3, Q1, not_42_out);
  not not_42 (not_42_out, Q0);
  and and_28 (and_28_out, Q3, Q2, Q1);
  not not_43 (not_43_out, Q1);
  and and_29 (and_29_out, not_43_out, not_44_out);
  not not_44 (not_44_out, Q0);
  and and_30 (and_30_out, Q2, not_45_out);
  not not_45 (not_45_out, Q0);
  and and_31 (and_31_out, Q3, Q1);
  and and_32 (and_32_out, Q3, Q2);
  not not_46 (not_46_out, Q3);
  not not_47 (not_47_out, Q2);
  not not_48 (not_48_out, Q0);
  not not_49 (not_49_out, Q3);
  not not_50 (not_50_out, Q1);
  not not_51 (not_51_out, Q0);
  not not_52 (not_52_out, Q3);
  not not_53 (not_53_out, Q3);
  not not_54 (not_54_out, Q2);
  not not_55 (not_55_out, Q1);
  not not_56 (not_56_out, Q3);
  not not_57 (not_57_out, Q1);
  not not_58 (not_58_out, Q0);
  not not_59 (not_59_out, Q1);
  and and_33 (and_33_out, not_59_out, not_60_out);
  not not_60 (not_60_out, Q0);
  not not_61 (not_61_out, Q2);
  and and_34 (and_34_out, not_61_out, Q1, Q0);
  not not_62 (not_62_out, Q3);
  and and_35 (and_35_out, not_62_out, Q2, not_63_out);
  not not_63 (not_63_out, Q0);
  and and_36 (and_36_out, Q2, not_64_out);
  not not_64 (not_64_out, Q1);
  and and_37 (and_37_out, Q3, not_65_out);
  not not_65 (not_65_out, Q2);
  not not_66 (not_66_out, Q3);
  and and_38 (and_38_out, not_66_out, not_67_out, Q0);
  not not_67 (not_67_out, Q1);
  not not_68 (not_68_out, Q2);
  and and_39 (and_39_out, not_68_out, Q1);
  and and_40 (and_40_out, Q2, not_69_out, Q0);
  not not_69 (not_69_out, Q1);
  and and_41 (and_41_out, Q3, Q1);
  not not_70 (not_70_out, Q3);
  and and_42 (and_42_out, not_70_out, not_71_out);
  not not_71 (not_71_out, Q2);
  not not_72 (not_72_out, Q3);
  and and_43 (and_43_out, not_72_out, Q0);
  not not_73 (not_73_out, Q2);
  and and_44 (and_44_out, not_73_out, Q0);
  not not_74 (not_74_out, Q3);
  and and_45 (and_45_out, not_74_out, Q1);
  and and_46 (and_46_out, Q3, not_75_out);
  not not_75 (not_75_out, Q1);
  and and_47 (and_47_out, Q3, Q2, not_76_out);
  not not_76 (not_76_out, Q0);
  not not_77 (not_77_out, Q3);
  and and_48 (and_48_out, not_77_out, not_78_out);
  not not_78 (not_78_out, Q2);
  not not_79 (not_79_out, Q2);
  and and_49 (and_49_out, not_79_out, Q0);
  not not_80 (not_80_out, Q1);
  and and_50 (and_50_out, not_80_out, Q0);
  and and_51 (and_51_out, Q2, Q1, not_81_out);
  not not_81 (not_81_out, Q0);
  and and_52 (and_52_out, Q3, not_82_out);
  not not_82 (not_82_out, Q1);
  not not_83 (not_83_out, Q3);
  not not_84 (not_84_out, Q2);
  not not_85 (not_85_out, Q1);
  not not_86 (not_86_out, Q2);
  not not_87 (not_87_out, Q0);
  not not_88 (not_88_out, Q3);
  not not_89 (not_89_out, Q1);
  not not_90 (not_90_out, Q0);
  not not_91 (not_91_out, Q0);
  or or_1 (S0, and_1_out, and_2_out, and_3_out);
  or or_2 (S1, and_4_out, Q1, and_5_out, Q3);
  or or_3 (S3, and_6_out, and_7_out, and_8_out);
  or or_4 (S4, and_9_out, and_10_out, and_11_out, Q3);
  and and_53 (and_53_out, not_9_out, not_10_out, not_11_out, Q0);
  or or_5 (S5, and_53_out, and_54_out);
  and and_54 (and_54_out, not_12_out, Q2, not_13_out, not_14_out);
  and and_55 (S6, not_15_out, not_16_out, not_17_out, Q0);
  or or_6 (S7, and_12_out, and_13_out, and_14_out, and_15_out);
  and and_56 (and_56_out, not_29_out, Q1, Q0);
  and and_57 (and_57_out, not_30_out, Q2, not_31_out, Q0);
  and and_58 (and_58_out, Q2, Q1, not_32_out);
  and and_59 (and_59_out, Q3, not_33_out);
  and and_60 (and_60_out, Q3, Q1);
  or or_7 (S10, and_22_out, Q1, and_23_out);
  or or_8 (S11, and_24_out, and_25_out, and_26_out, and_27_out, and_28_out);
  or or_9 (S12, and_29_out, and_30_out, and_31_out, and_32_out);
  and and_61 (and_61_out, not_46_out, not_47_out, Q1, not_48_out);
  and and_62 (and_62_out, not_49_out, Q2, not_50_out, not_51_out);
  or or_10 (S13, and_61_out, and_62_out, and_63_out);
  and and_63 (and_63_out, not_52_out, Q2, Q1, Q0);
  and and_64 (and_64_out, not_53_out, not_54_out, not_55_out, Q0);
  or or_11 (S14, and_64_out, and_65_out);
  and and_65 (and_65_out, not_56_out, Q2, not_57_out, not_58_out);
  or or_12 (S15, and_33_out, and_34_out, and_35_out, and_36_out, and_37_out);
  or or_13 (S16, and_38_out, and_39_out, and_40_out, and_41_out);
  or or_14 (S18, and_48_out, and_49_out, and_50_out, and_51_out, and_52_out);
  and and_66 (and_66_out, not_83_out, not_84_out, not_85_out, Q0);
  and and_67 (and_67_out, not_86_out, Q1, not_87_out);
  and and_68 (and_68_out, not_88_out, Q2, not_89_out, not_90_out);
  and and_69 (and_69_out, Q3, Q1, not_91_out);
  or or_15 (S8, and_16_out, and_17_out, and_18_out, and_19_out, and_20_out, and_21_out);
  or or_16 (S9, and_56_out, and_57_out, and_58_out, and_59_out, and_60_out);
  or or_17 (S17, and_42_out, and_43_out, and_44_out, and_45_out, and_46_out, and_47_out);
  or or_18 (S19, and_66_out, and_67_out, and_68_out, and_69_out);

  assign S2 = 1'b1;
endmodule

module cont (
  input  in_1,
  output out_2,
  output out_3,
  output out_4,
  output out_5
);

  wire clock_1_out;

  Clock clock_1 (.out(clock_1_out));
  J_K_Flip_Flop #(.trigger("falling")) j_k_ff_1 (
    .J(1'b1), .clk(clock_1_out), .K(1'b1), .Q(out_2), .reset(in_1));  // open: Qn, preset, en
  J_K_Flip_Flop #(.trigger("falling")) j_k_ff_2 (
    .J(1'b1), .clk(out_2), .K(1'b1), .Q(out_3), .reset(in_1));  // open: Qn, preset, en
  J_K_Flip_Flop #(.trigger("falling")) j_k_ff_3 (
    .J(1'b1), .clk(out_3), .K(1'b1), .Q(out_4), .reset(in_1));  // open: Qn, preset, en
  J_K_Flip_Flop #(.trigger("falling")) j_k_ff_4 (
    .J(1'b1), .clk(out_4), .K(1'b1), .Q(out_5), .reset(in_1));  // open: Qn, preset, en
endmodule
