// Logisim project display-4x5.circ as structural Verilog: 1 circuit, main circuit main
module main (
  output _0,
  output _3,
  output _4,
  output _7,
  output out_5,
  output out_6,
  output _8,
  output _11,
  output _12,
  output out_10,
  output out_11,
  output _15,
  output _9,
  output _10,
  output out_15,
  output out_16,
  output _16,
  output _19,
  output out_19,
  output out_20
);


  // Notes on the sheet:
  //   5
  //   1
  //   17
  //   13
  //   6
  //   2
  //   18
  //   14
endmodule
